# Fritzing sketch Sketch_BluetoothHC05_Fritzing (saved by Fritzing 0.9.4)
breadboards: 1

parts:
  Componente1 = Bluetooth HC-05 Macho
  Componente2 = Arduino Uno (Rev3) - ICSP
  LED1 = LED - 5mm [color="Red (633nm)" package="5 mm [THT]"]
  R1 = Resistor [tolerance=±5% resistance=220 package=THT]

nets:
  N1: Componente1.TXD, Componente2.D0/RX
  N2: Componente1.RXD, Componente2.D1/TX
  VCC: Componente1.VCC, Componente2.5V
  GND: Componente1.GND, Componente2.GND, LED1.cathode
  N3: Componente2.D13/SCK, R1.Pin_1
